# Fritzing sketch LectorRFID_FFZ (saved by Fritzing 0.9.3b)

parts:
  Componente2 = Arduino Uno (Rev3)
  RFID-RC522 = RFID-RC522-v2

nets:
  N1: Componente2.D9_PWM, RFID-RC522.RST
  N2: Componente2.D10_PWM/SS, RFID-RC522.SDA
  N3: Componente2.D11_PWM/MOSI, RFID-RC522.MOSI
  N4: Componente2.D12/MISO, RFID-RC522.MISO
  N5: Componente2.D13/SCK, RFID-RC522.SCK
  3V3: Componente2.3V3, RFID-RC522.3.3V
  GND: Componente2.GND, RFID-RC522.GND

custom parts:
  RFID-RC522-v2: A simple China made RFID-RC522 Reader; do check the pin labels, as this is a MFRC522 based clone.
